# Fritzing sketch wetplant (saved by Fritzing 1.0.4)

parts:
  MCU1 = Raspberry Pi Zero
  moisture_sensor = Soil Moisture Sensor
  power = ADS1015
  JP1 = USB_MICROB_PLUG [package=micro-b-th]

nets:
  N1: MCU1.pin_1, MCU1.pin_17, power.VDD
  VCC: MCU1.pin_2, moisture_sensor.VCC, JP1.VCC
  N2: MCU1.pin_3, power.SDA
  N3: MCU1.pin_5, power.SCL
  GND: MCU1.pin_9, MCU1.pin_39, moisture_sensor.GND, power.GND, JP1.GND
  N4: moisture_sensor.SIG, power.A0

custom parts:
  ADS1015: ADC ADS1015
